# Fritzing sketch final (saved by Fritzing 1.0.1rc)
circuit board: 8.46667cm x 5.64444cm
breadboards: 1

parts:
  RHT1 = Humidity and Temperature Sensor RHT03
  R1 = Resistor [tolerance=±5% resistance=220 package="0402 [SMD]"]
  J1 = Raspberry Pi Header 40pin [form="♂ (male)" package=THT]
  J2 = Raspberry Pi Header 40pin [form="♂ (male)" package=THT]
  M1 = DC Motor [voltage_(max)=6V voltage_(min)=3V]
  IC1 = L293D [package=THT]
  R2 = Resistor [tolerance=±5% power=0.25W resistance=220 package=THT]
  LED2 = LED - 5mm [color="Red (633nm)" current=0.030A package="5 mm [THT]"]
  Mod1 = Amica NodeMCU DEVKIT 1.0
  Part1 = RFID-RC522-v2
  R3 = Resistor [tolerance=±5% power=0.25W resistance=220 package=THT]
  R4 = Photocell (LDR) [power=0.25W dark_resistance_@0.01lx=300kΩ light_resistance_@100lx=400Ω luminance=10lx package=THT]
  VCC1 = Battery block 9V

nets (from the breadboard view):
  3V3: RHT1.Vcc, RHT1.Data-signal, RHT1.GND_2, R1.Pin_0, J2.3v3, J2.3V3, R4.pin_1
  N1: R1.Pin_1, J2.GIPO5
  N2: J1.GND, LED2.cathode, R3.Pin_0
  N3: J1.GIPO12, R2.Pin_0
  N4: J2.GND, M1.pin_2, IC1.0V, VCC1.-
  N5: J2.GIPO17, IC1.+Vmotor
  N6: J2.GIPO27, IC1.Out_1_(_Controlled_by_Enable_1_)
  N7: J2.GIPO22, IC1.In_1
  N8: M1.pin_1, IC1.In_2
  N9: IC1.+V, VCC1.+
  N10: R2.Pin_1, LED2.anode
  N11: Mod1.pin1, Mod1.pin_10, Mod1.pin_26
  N12: Mod1.pin2, Mod1.pin_9, Mod1.pin_25, Mod1.pin_29, Part1.GND
  N13: Mod1.pin5, Part1.SDA
  N14: Mod1.pin6, Part1.MOSI
  N15: Mod1.pin7, Part1.MISO
  N16: Mod1.pin8, Part1.SCK
  N17: Mod1.pin_15, Part1.RST
  N18: Mod1.pin_16, R3.Pin_1, R4.pin_0
  N19: Mod1.pin_30, Part1.3.3V

custom parts:
  Raspberry Pi Header 40pin: Raspberry Pi 40 pin header - for creating your own shields.
  RFID-RC522-v2: A simple China made RFID-RC522 Reader; do check the pin labels, as this is a MFRC522 based clone.
